// Logisim project SoC_分支冒险.circ as structural Verilog: 19 circuits, main circuit Branch
module cpu (
  input  [31:0] in_1,
  input  [31:0] in_2,
  input  in_3,
  input  in_4,
  output out_5,
  output out_6,
  output out_7,
  output [31:0] out_8,
  output [31:0] out_9,
  output [31:0] out_10,
  output [31:0] out_11,
  output [31:0] out_12,
  output [31:0] out_13,
  output [31:0] out_14,
  output [31:0] out_15,
  output [31:0] out_16,
  output [31:0] out_17,
  output [31:0] out_18
);

  wire and_1_out, and_2_out, and_3_out, and_4_out, Branch, branch_1_breq, branch_1_brlt,
       controlmodel_1_alusela, controlmodel_1_aluselb, controlmodel_1_beq, controlmodel_1_bge,
       controlmodel_1_bgeu, controlmodel_1_blt, controlmodel_1_bltu, controlmodel_1_bne, controlmodel_1_brun,
       controlmodel_1_pcsel, controlmodel_1_regwrite, En, or_1_out, or_2_out;
  wire [1:0] controlmodel_1_wbsel;
  wire [2:0] controlmodel_1_immsel;
  wire [3:0] controlmodel_1_aluop;
  wire [31:0] adder_1_out, immmodel_1_immdiate, multiplexer_1_out, multiplexer_2_out, multiplexer_3_out,
       multiplexer_4_out, regfile_1_read_data_1;

  Adder #(.width(32)) adder_1 (.a(out_16), .b(32'h4), .out(adder_1_out));  // open: cin, cout
  Multiplexer #(.select(1), .width(32), .disabled("Z"), .enable("false")) multiplexer_1 (
    .in0(adder_1_out), .in1(out_17), .out(multiplexer_1_out), .sel(Branch));
  Register #(.width(32), .trigger("rising"), .Select("low")) PC (
    .D(multiplexer_1_out), .en(En), .Q(out_16), .clk(in_3));  // open: clr
  Comparator #(.width(32), .mode("unsigned")) comparator_1 (.a(in_1), .b({32{1'b0}}), .eq(out_7));  // open: gt, lt
  // Probe on adder_1_out
  // Probe on out_16
  nor nor_1 (En, out_7, in_4);
  Pull_Resistor #(.pull(0)) pull_resistor_1 (.node(in_4));
  // Probe on in_1
  ControlModel controlmodel_1 (
    .ALUOP(controlmodel_1_aluop), .ALUSelA(controlmodel_1_alusela), .PCSel(controlmodel_1_pcsel),
    .WBSel(controlmodel_1_wbsel), .ALUSelB(controlmodel_1_aluselb), .MemWrite(out_6),
    .ImmSel(controlmodel_1_immsel), .Instruction(in_1), .BrUN(controlmodel_1_brun),
    .RegWrite(controlmodel_1_regwrite), .MemRead(out_5), .BEQ(controlmodel_1_beq), .BNE(controlmodel_1_bne),
    .BGE(controlmodel_1_bge), .BLT(controlmodel_1_blt), .BLTU(controlmodel_1_bltu), .BGEU(controlmodel_1_bgeu));
  ImmModel immmodel_1 (.Immdiate(immmodel_1_immdiate), .INSTRUCTION(in_1), .InstructionType(controlmodel_1_immsel));
  RegFile regfile_1 (
    .rs1(in_1[19:15]), .rs2(in_1[24:20]), .rd(in_1[11:7]), .Write_Data(multiplexer_4_out),
    .RegWEn(controlmodel_1_regwrite), .clk(in_3), .Read_Data_1(regfile_1_read_data_1), .Read_Data_2(out_18),
    .ra(out_8), .sp(out_9), .t0(out_10), .t1(out_11), .t2(out_12), .s0(out_13), .s1(out_14), .a0(out_15));
  or or_1 (or_1_out, controlmodel_1_blt, controlmodel_1_bltu);
  or or_2 (or_2_out, controlmodel_1_bge, controlmodel_1_bgeu);
  Branch branch_1 (
    .BrEQ(branch_1_breq), .RS2(out_18), .BrUN(controlmodel_1_brun), .BrLT(branch_1_brlt),
    .RS1(regfile_1_read_data_1));
  Multiplexer #(.select(1), .width(32), .disabled("Z"), .enable("false")) multiplexer_2 (
    .in0(regfile_1_read_data_1), .in1(out_16), .out(multiplexer_2_out), .sel(controlmodel_1_alusela));
  Multiplexer #(.select(1), .width(32), .disabled("Z"), .enable("false")) multiplexer_3 (
    .in0(out_18), .in1(immmodel_1_immdiate), .out(multiplexer_3_out), .sel(controlmodel_1_aluselb));
  and and_1 (and_1_out, branch_1_breq, controlmodel_1_beq);
  and and_2 (and_2_out, ~branch_1_breq, controlmodel_1_bne);  // AND_Gate
  and and_3 (and_3_out, branch_1_brlt, or_1_out);
  and and_4 (and_4_out, ~branch_1_brlt, or_2_out);  // AND_Gate
  or or_3 (Branch, controlmodel_1_pcsel, and_1_out, and_2_out, and_3_out, and_4_out);
  // Probe on out_17
  AluModel alumodel_1 (.Result(out_17), .ALUSel(controlmodel_1_aluop), .B(multiplexer_3_out), .A(multiplexer_2_out));
  // Probe on out_18
  // Probe on in_2
  Multiplexer #(.select(2), .width(32), .disabled("Z"), .enable("false")) multiplexer_4 (
    .in0(adder_1_out), .in1(out_17), .in2(in_2), .out(multiplexer_4_out), .sel(controlmodel_1_wbsel));  // open: in3

  // Other names for the same wires on the sheet: a0[31:0] = out_15; clk = in_3; fetch_addr[31:0] = out_16;
  //   halt = out_7; Instruction[31:0] = in_1; MemR = out_5; MemW = out_6; Miss = in_4; ra[31:0] = out_8;
  //   ReadData[31:0] = in_2; s0[31:0] = out_13; s1[31:0] = out_14; sp[31:0] = out_9; t0[31:0] = out_10;
  //   t1[31:0] = out_11; t2[31:0] = out_12; WriteAddr[31:0] = out_17; WriteData[31:0] = out_18

  // Notes on the sheet:
  //   PC
  //   PC+4
  //   ALU_Result
  //   ALU_Result
  //   输入引脚区
  //   输出引脚区
  //   ALU_Result
  //   PC+4
  //   WriteData
  //   WBSel
endmodule

module SoC (
  input  \清屏信号 ,
  input  \清空缓存 
);

  wire busmodel_1_ioen, busmodel_1_memr, busmodel_1_memw, busmodel_1_out_8, clk, halt, keyboard_1_avail,
       keyttydriver_1_clock, keyttydriver_1_ttyenable, Miss, not_1_out, or_1_out, three_stage_cpu_1_out_5,
       three_stage_cpu_1_out_6, undriven;
  wire [3:0] leddriver_1_displaydata_2, leddriver_1_displaydata_3, leddriver_1_displaydata_4,
       leddriver_1_displaydata_5;
  wire [6:0] keyboard_1_data, keyttydriver_1_ttydata;
  wire [11:0] busmodel_1_ioaddr12;
  wire [15:0] leddriver_1_displaydata, MissNumber, \总周期数 ;
  wire [31:0] busmodel_1_iowritedata, busmodel_1_memaddr, busmodel_1_memwritedata, busmodel_1_readdata,
       dmem_1_read_data, Instruction, keyttydriver_1_ioread, three_stage_cpu_1_out_16,
       three_stage_cpu_1_out_17, three_stage_cpu_1_out_18;

  // Probe on three_stage_cpu_1_out_16
  Clock #(.highDuration(1), .lowDuration(1)) clock_1 (.out(clk));
  // Probe on \总周期数 
  // Probe on MissNumber
  Hex_Digit_Display hex_digit_display_1 (.value(leddriver_1_displaydata_5));  // open: dp
  Hex_Digit_Display hex_digit_display_2 (.value(leddriver_1_displaydata_3));  // open: dp
  Hex_Digit_Display hex_digit_display_3 (.value(leddriver_1_displaydata_4));  // open: dp
  IMEM imem_1 (.Instruction(Instruction), .Program_counter(three_stage_cpu_1_out_16));
  // Probe on Instruction
  Hex_Digit_Display hex_digit_display_4 (.value(leddriver_1_displaydata_2));  // open: dp
  Hex_Digit_Display hex_digit_display_5 (.value(leddriver_1_displaydata[15:12]));  // open: dp
  LedDriver leddriver_1 (
    .IOWriteData(busmodel_1_iowritedata), .IOAddr12(busmodel_1_ioaddr12), .IOEn(busmodel_1_ioen),
    .DisplayData({leddriver_1_displaydata_5, leddriver_1_displaydata_4, leddriver_1_displaydata_3, leddriver_1_displaydata_2, leddriver_1_displaydata}),
    .in_4(clk));
  Hex_Digit_Display hex_digit_display_6 (.value(leddriver_1_displaydata[7:4]));  // open: dp
  Hex_Digit_Display hex_digit_display_7 (.value(leddriver_1_displaydata[11:8]));  // open: dp
  // Probe on Miss
  Hex_Digit_Display hex_digit_display_8 (.value(leddriver_1_displaydata[3:0]));  // open: dp
  // Probe on busmodel_1_iowritedata
  or or_1 (or_1_out, halt, Miss);
  not not_1 (not_1_out, or_1_out);
  Counter #(.width(16), .max('hffff), .ongoal("wrap"), .trigger("rising"), .behavior("old")) counter_1 (
    .count(not_1_out), .Q(\总周期数 ), .clk(clk));  // open: load, D, carry, clr, preset
  // Probe on busmodel_1_ioaddr12
  Three_stage_CPU three_stage_cpu_1 (
    .in_1(Instruction), .in_2(busmodel_1_readdata), .out_5(three_stage_cpu_1_out_5),
    .out_6(three_stage_cpu_1_out_6), .out_16(three_stage_cpu_1_out_16), .out_17(three_stage_cpu_1_out_17),
    .out_18(three_stage_cpu_1_out_18), .in_3(clk), .out_7(halt), .in_4(undriven));  // open: out_8, out_9, out_10, out_11, out_12, out_13, out_14, out_15
  TTY #(.Char_bit_width(7), .rows(16), .cols(40), .trigger("rising")) tty_1 (
    .data(keyttydriver_1_ttydata), .clk(keyttydriver_1_clock), .we(keyttydriver_1_ttyenable), .clr(\清屏信号 ));
  BusModel busmodel_1 (
    .ReadData(busmodel_1_readdata), .IOWriteData(busmodel_1_iowritedata),
    .WriteAddr(three_stage_cpu_1_out_17), .MemRead(dmem_1_read_data), .IOAddr12(busmodel_1_ioaddr12),
    .WriteData(three_stage_cpu_1_out_18), .R(three_stage_cpu_1_out_5), .IORead(keyttydriver_1_ioread),
    .IOEn(busmodel_1_ioen), .MemAddr(busmodel_1_memaddr), .MemR(busmodel_1_memr),
    .MemWriteData(busmodel_1_memwritedata), .out_8(busmodel_1_out_8), .W(three_stage_cpu_1_out_6),
    .MemW(busmodel_1_memw));
  Keyboard #(.Char_bit_width(7), .buflen(32), .trigger("rising")) keyboard_1 (
    .clk(keyttydriver_1_clock), .re(1'b1), .clr(\清空缓存 ), .avail(keyboard_1_avail), .data(keyboard_1_data));
  KeyTTYDriver keyttydriver_1 (
    .TTYData(keyttydriver_1_ttydata), .IOWriteData(busmodel_1_iowritedata),
    .TTYEnable(keyttydriver_1_ttyenable), .IOAddr12(busmodel_1_ioaddr12), .KeyValue(keyboard_1_data),
    .IORead(keyttydriver_1_ioread), .IOEn(busmodel_1_ioen), .clk(clk), .clock(keyttydriver_1_clock),
    .in_2(busmodel_1_out_8), .KeyEn(keyboard_1_avail));
  DMEM dmem_1 (
    .Write_En(busmodel_1_memw), .clk(clk), .Read_Data(dmem_1_read_data), .Address(busmodel_1_memaddr),
    .Write_Data(busmodel_1_memwritedata), .Read_En(busmodel_1_memr), .MissNubmer(MissNumber));

  // Notes on the sheet:
  //   时钟
  //   总周期数
  //   Cache缺失次数
  //   7-Segment驱动
  //   I/O总线
  //   键盘
  //   TTY 终端
  //   TTY和Keyboard驱动
endmodule

module Three_stage_CPU (
  input  [31:0] in_1,
  input  [31:0] in_2,
  input  in_3,
  input  in_4,
  output out_5,
  output out_6,
  output out_7,
  output [31:0] out_8,
  output [31:0] out_9,
  output [31:0] out_10,
  output [31:0] out_11,
  output [31:0] out_12,
  output [31:0] out_13,
  output [31:0] out_14,
  output [31:0] out_15,
  output [31:0] out_16,
  output [31:0] out_17,
  output [31:0] out_18
);

  wire _0Branch, and_1_out, and_2_out, and_3_out, and_4_out, Branch, branch_1_breq, branch_1_brlt,
       controlmodel_1_alusela, controlmodel_1_aluselb, controlmodel_1_beq, controlmodel_1_bge,
       controlmodel_1_bgeu, controlmodel_1_blt, controlmodel_1_bltu, controlmodel_1_bne, controlmodel_1_brun,
       controlmodel_1_memread, controlmodel_1_memwrite, controlmodel_1_pcsel, controlmodel_1_regwrite, En,
       id_ex_1_out_21, id_ex_1_out_22, id_ex_1_out_23, id_ex_1_out_24, id_ex_1_out_25, id_ex_1_out_26,
       id_ex_1_out_27, id_ex_1_out_32, id_ex_1_out_33, id_ex_1_out_34, id_ex_1_out_35, or_1_out, or_2_out,
       or_3_out, or_4_out, or_5_out, PC_2_q, undriven;
  wire [1:0] controlmodel_1_wbsel, id_ex_1_out_28;
  wire [2:0] controlmodel_1_immsel;
  wire [3:0] controlmodel_1_aluop, id_ex_1_out_31;
  wire [31:0] adder_1_out, id_ex_1_out_36, if_id_1_id_instruction, immmodel_1_immdiate, Ins_q,
       multiplexer_1_out, multiplexer_3_out, multiplexer_4_out, multiplexer_5_out, multiplexer_7_out,
       multiplexer_8_out, regfile_1_read_data_1, subtractor_1_out, subtractor_2_out;

  Adder #(.width(32)) adder_1 (.a(out_16), .b(32'h4), .out(adder_1_out));  // open: cin, cout
  Multiplexer #(.select(1), .width(32), .disabled("Z"), .enable("false")) multiplexer_1 (
    .in0(adder_1_out), .in1(out_17), .out(multiplexer_1_out), .sel(Branch));
  Comparator #(.width(32), .mode("unsigned")) comparator_1 (.a(in_1), .b({32{1'b0}}), .eq(out_7));  // open: gt, lt
  // Probe on out_16
  Register #(.width(32), .trigger("falling"), .Select("low")) PC (
    .D(multiplexer_1_out), .en(En), .Q(out_16), .clk(in_3));  // open: clr
  nor nor_1 (En, 1'b0, in_4);
  Pull_Resistor #(.pull(0)) pull_resistor_1 (.node(in_4));
  Comparator #(.width(32), .mode("unsigned")) comparator_2 (.a(out_16), .b({32{1'b0}}), .eq(_0Branch));  // open: gt, lt
  // Probe on in_1
  or or_1 (or_1_out, 1'b0, PC_2_q);
  Multiplexer #(.select(1), .width(1), .disabled("Z"), .enable("false")) multiplexer_2 (
    .in1(1'b0), .out(Branch), .sel(_0Branch));  // open: in0
  IF_ID if_id_1 (
    .IF_Instruction(in_1), .in_2(in_3), .ID_Instruction(if_id_1_id_instruction), .in_4(or_1_out));  // open: IF_PC, ID_PC
  Register #(.width(32), .trigger("rising"), .Select("low")) Ins (
    .D(if_id_1_id_instruction), .en(1'b1), .Q(Ins_q), .clk(in_3), .clr(or_1_out));
  ControlModel controlmodel_1 (
    .ALUOP(controlmodel_1_aluop), .ALUSelA(controlmodel_1_alusela), .PCSel(controlmodel_1_pcsel),
    .WBSel(controlmodel_1_wbsel), .ALUSelB(controlmodel_1_aluselb), .MemWrite(controlmodel_1_memwrite),
    .ImmSel(controlmodel_1_immsel), .Instruction(if_id_1_id_instruction), .BrUN(controlmodel_1_brun),
    .RegWrite(controlmodel_1_regwrite), .MemRead(controlmodel_1_memread), .BEQ(controlmodel_1_beq),
    .BNE(controlmodel_1_bne), .BGE(controlmodel_1_bge), .BLT(controlmodel_1_blt), .BLTU(controlmodel_1_bltu),
    .BGEU(controlmodel_1_bgeu));
  or or_2 (or_2_out, 1'b0, PC_2_q);
  ID_EX id_ex_1 (
    .in_2(controlmodel_1_pcsel), .in_3(controlmodel_1_beq), .in_4(controlmodel_1_bne),
    .in_5(controlmodel_1_blt), .in_6(controlmodel_1_bltu), .in_7(controlmodel_1_bge),
    .in_8(controlmodel_1_bgeu), .in_9(controlmodel_1_wbsel), .in_10(controlmodel_1_memread),
    .in_11(controlmodel_1_memwrite), .in_12(controlmodel_1_aluop), .in_13(controlmodel_1_aluselb),
    .in_14(controlmodel_1_alusela), .in_15(controlmodel_1_brun), .in_16(controlmodel_1_regwrite),
    .in_17(in_3), .in_19(immmodel_1_immdiate), .out_36(id_ex_1_out_36), .out_21(id_ex_1_out_21),
    .out_22(id_ex_1_out_22), .out_23(id_ex_1_out_23), .out_24(id_ex_1_out_24), .out_25(id_ex_1_out_25),
    .out_26(id_ex_1_out_26), .out_27(id_ex_1_out_27), .out_28(id_ex_1_out_28), .out_29(out_5),
    .out_30(out_6), .out_31(id_ex_1_out_31), .out_32(id_ex_1_out_32), .out_33(id_ex_1_out_33),
    .out_34(id_ex_1_out_34), .out_35(id_ex_1_out_35), .in_18(or_2_out));  // open: in_1, out_20
  ImmModel immmodel_1 (
    .Immdiate(immmodel_1_immdiate), .INSTRUCTION(if_id_1_id_instruction),
    .InstructionType(controlmodel_1_immsel));
  RegFile regfile_1 (
    .rs1(Ins_q[19:15]), .rs2(Ins_q[24:20]), .rd(Ins_q[11:7]), .Write_Data(subtractor_2_out),
    .RegWEn(id_ex_1_out_35), .clk(in_3), .Read_Data_1(regfile_1_read_data_1), .Read_Data_2(out_18),
    .ra(out_8), .sp(out_9), .t0(out_10), .t1(out_11), .t2(out_12), .s0(out_13), .s1(out_14), .a0(out_15));
  Multiplexer #(.select(1), .width(32), .disabled("Z"), .enable("false")) multiplexer_3 (
    .in0({32{1'b0}}), .in1(32'h8), .out(multiplexer_3_out), .sel(id_ex_1_out_33));
  or or_3 (or_3_out, id_ex_1_out_26, id_ex_1_out_27);
  Subtractor #(.width(32)) subtractor_1 (.a(out_16), .b(multiplexer_3_out), .out(subtractor_1_out));  // open: bin, bout
  or or_4 (or_4_out, id_ex_1_out_24, id_ex_1_out_25);
  Branch branch_1 (
    .BrEQ(branch_1_breq), .RS2(out_18), .BrUN(id_ex_1_out_34), .BrLT(branch_1_brlt),
    .RS1(regfile_1_read_data_1));
  Multiplexer #(.select(1), .width(32), .disabled("Z"), .enable("false")) multiplexer_4 (
    .in0(regfile_1_read_data_1), .in1(subtractor_1_out), .out(multiplexer_4_out), .sel(id_ex_1_out_33));
  Multiplexer #(.select(1), .width(32), .disabled("Z"), .enable("false")) multiplexer_5 (
    .in0(out_18), .in1(id_ex_1_out_36), .out(multiplexer_5_out), .sel(id_ex_1_out_32));
  and and_1 (and_1_out, branch_1_breq, id_ex_1_out_22);
  and and_2 (and_2_out, ~branch_1_breq, id_ex_1_out_23);  // AND_Gate
  and and_3 (and_3_out, branch_1_brlt, or_4_out);
  and and_4 (and_4_out, ~branch_1_brlt, or_3_out);  // AND_Gate
  or or_5 (or_5_out, id_ex_1_out_21, and_1_out, and_2_out, and_3_out, and_4_out);
  // Probe on out_17
  AluModel alumodel_1 (.Result(out_17), .ALUSel(id_ex_1_out_31), .B(multiplexer_5_out), .A(multiplexer_4_out));
  Multiplexer #(.select(1), .width(1), .disabled("Z"), .enable("false")) multiplexer_6 (
    .in0(or_5_out), .out(Branch), .sel(_0Branch));  // open: in1
  // Probe on out_18
  Register #(.width(1), .trigger("falling"), .Select("low")) PC_2 (
    .D(Branch), .en(1'b1), .Q(PC_2_q), .clk(in_3), .preset(undriven));  // open: clr, cs
  // Probe on in_2
  Multiplexer #(.select(2), .width(32), .disabled("Z"), .enable("false")) multiplexer_7 (
    .in0(32'h8), .in1({32{1'b0}}), .in2({32{1'b0}}), .in3({32{1'b0}}), .out(multiplexer_7_out),
    .sel(id_ex_1_out_28));
  Subtractor #(.width(32)) subtractor_2 (
    .a(multiplexer_8_out), .b(multiplexer_7_out), .out(subtractor_2_out));  // open: bin, bout
  Multiplexer #(.select(2), .width(32), .disabled("Z"), .enable("false")) multiplexer_8 (
    .in0(adder_1_out), .in1(out_17), .in2(in_2), .out(multiplexer_8_out), .sel(id_ex_1_out_28));  // open: in3

  // Other names for the same wires on the sheet: a0[31:0] = out_15; clk = in_3; fetch_addr[31:0] = out_16;
  //   halt = out_7; Instruction[31:0] = in_1; MemR = out_5; MemW = out_6; Miss = in_4; ra[31:0] = out_8;
  //   ReadData[31:0] = in_2; s0[31:0] = out_13; s1[31:0] = out_14; sp[31:0] = out_9; t0[31:0] = out_10;
  //   t1[31:0] = out_11; t2[31:0] = out_12; WriteAddr[31:0] = out_17; WriteData[31:0] = out_18

  // Notes on the sheet:
  //   ALU_Result
  //   输入引脚区
  //   请勿增改引脚，请勿修改子电路封装
  //   输出引脚区
  //   ALU_Result
  //   PC+4
  //   WBSel
  //   WriteData
endmodule

module RegFile (
  input  [4:0] rs1,
  input  [4:0] rs2,
  input  [4:0] rd,
  input  [31:0] Write_Data,
  input  RegWEn,
  input  clk,
  output [31:0] ra,
  output [31:0] sp,
  output [31:0] t0,
  output [31:0] t1,
  output [31:0] t2,
  output [31:0] s0,
  output [31:0] s1,
  output [31:0] a0,
  output [31:0] Read_Data_1,
  output [31:0] Read_Data_2
);

  wire write_en1, write_en2, write_en3, write_en4, write_en5, write_en6, write_en7, write_en8, write_en9,
       write_en10, write_en11, write_en12, write_en13, write_en14, write_en15, write_en16, write_en17,
       write_en18, write_en19, write_en20, write_en21, write_en22, write_en23, write_en24, write_en25,
       write_en26, write_en27, write_en28, write_en29, write_en30, write_en31;
  wire [31:0] x3, x4, x11, x12, x13, x14, x15, x16, x17, x18, x19, x20, x21, x22, x23, x24, x25, x26, x27,
       x28, x29, x30, x31;

  Pull_Resistor #(.pull(0)) pull_resistor_1 (.node(write_en1));
  Register #(.width(32), .trigger("rising"), .Select("low")) register_1 (
    .D(Write_Data), .en(write_en8), .Q(s0), .clk(clk));  // open: clr
  Register #(.width(32), .trigger("rising"), .Select("low")) register_2 (
    .D(Write_Data), .en(write_en16), .Q(x16), .clk(clk));  // open: clr
  Register #(.width(32), .trigger("rising"), .Select("low")) register_3 (
    .D(Write_Data), .en(write_en24), .Q(x24), .clk(clk));  // open: clr
  Pull_Resistor #(.pull(0)) pull_resistor_2 (.node(write_en3));
  Pull_Resistor #(.pull(0)) pull_resistor_3 (.node(write_en2));
  Pull_Resistor #(.pull(0)) pull_resistor_4 (.node(write_en4));
  Pull_Resistor #(.pull(0)) pull_resistor_5 (.node(write_en5));
  // Probe on ra
  Register #(.width(32), .trigger("rising"), .Select("low")) register_4 (
    .D(Write_Data), .en(write_en1), .Q(ra), .clk(clk));  // open: clr
  Register #(.width(32), .trigger("rising"), .Select("low")) register_5 (
    .D(Write_Data), .en(write_en9), .Q(s1), .clk(clk));  // open: clr
  Register #(.width(32), .trigger("rising"), .Select("low")) register_6 (
    .D(Write_Data), .en(write_en17), .Q(x17), .clk(clk));  // open: clr
  Register #(.width(32), .trigger("rising"), .Select("low")) register_7 (
    .D(Write_Data), .en(write_en25), .Q(x25), .clk(clk));  // open: clr
  Pull_Resistor #(.pull(0)) pull_resistor_6 (.node(write_en7));
  Pull_Resistor #(.pull(0)) pull_resistor_7 (.node(write_en6));
  Pull_Resistor #(.pull(0)) pull_resistor_8 (.node(write_en8));
  Pull_Resistor #(.pull(0)) pull_resistor_9 (.node(write_en9));
  // Probe on Write_Data
  // Probe on write_en18
  Pull_Resistor #(.pull(0)) pull_resistor_10 (.node(write_en11));
  Pull_Resistor #(.pull(0)) pull_resistor_11 (.node(write_en10));
  Register #(.width(32), .trigger("rising"), .Select("low")) register_8 (
    .D(Write_Data), .en(write_en2), .Q(sp), .clk(clk));  // open: clr
  Register #(.width(32), .trigger("rising"), .Select("low")) register_9 (
    .D(Write_Data), .en(write_en10), .Q(a0), .clk(clk));  // open: clr
  Register #(.width(32), .trigger("rising"), .Select("low")) register_10 (
    .D(Write_Data), .en(write_en18), .Q(x18), .clk(clk));  // open: clr
  // Probe on x18
  Register #(.width(32), .trigger("rising"), .Select("low")) register_11 (
    .D(Write_Data), .en(write_en26), .Q(x26), .clk(clk));  // open: clr
  Pull_Resistor #(.pull(0)) pull_resistor_12 (.node(write_en12));
  Pull_Resistor #(.pull(0)) pull_resistor_13 (.node(write_en13));
  Pull_Resistor #(.pull(0)) pull_resistor_14 (.node(write_en15));
  Pull_Resistor #(.pull(0)) pull_resistor_15 (.node(write_en14));
  Register #(.width(32), .trigger("rising"), .Select("low")) register_12 (
    .D(Write_Data), .en(write_en3), .Q(x3), .clk(clk));  // open: clr
  Register #(.width(32), .trigger("rising"), .Select("low")) register_13 (
    .D(Write_Data), .en(write_en11), .Q(x11), .clk(clk));  // open: clr
  Register #(.width(32), .trigger("rising"), .Select("low")) register_14 (
    .D(Write_Data), .en(write_en19), .Q(x19), .clk(clk));  // open: clr
  Register #(.width(32), .trigger("rising"), .Select("low")) register_15 (
    .D(Write_Data), .en(write_en27), .Q(x27), .clk(clk));  // open: clr
  Pull_Resistor #(.pull(0)) pull_resistor_16 (.node(write_en16));
  Pull_Resistor #(.pull(0)) pull_resistor_17 (.node(write_en17));
  Pull_Resistor #(.pull(0)) pull_resistor_18 (.node(write_en18));
  Pull_Resistor #(.pull(0)) pull_resistor_19 (.node(write_en19));
  Register #(.width(32), .trigger("rising"), .Select("low")) register_16 (
    .D(Write_Data), .en(write_en4), .Q(x4));  // open: clk, clr
  Register #(.width(32), .trigger("rising"), .Select("low")) register_17 (
    .D(Write_Data), .en(write_en12), .Q(x12), .clk(clk));  // open: clr
  Register #(.width(32), .trigger("rising"), .Select("low")) register_18 (
    .D(Write_Data), .en(write_en20), .Q(x20), .clk(clk));  // open: clr
  Register #(.width(32), .trigger("rising"), .Select("low")) register_19 (
    .D(Write_Data), .en(write_en28), .Q(x28), .clk(clk));  // open: clr
  Pull_Resistor #(.pull(0)) pull_resistor_20 (.node(write_en20));
  Pull_Resistor #(.pull(0)) pull_resistor_21 (.node(write_en21));
  Pull_Resistor #(.pull(0)) pull_resistor_22 (.node(write_en22));
  Pull_Resistor #(.pull(0)) pull_resistor_23 (.node(write_en23));
  Decoder #(.select(5), .tristate("false"), .disabled("Z"), .enable("true")) decoder_1 (
    .out1(write_en1), .out2(write_en2), .out3(write_en3), .out4(write_en4), .out5(write_en5),
    .out6(write_en6), .out7(write_en7), .out8(write_en8), .out9(write_en9), .out10(write_en10),
    .out11(write_en11), .out12(write_en12), .out13(write_en13), .out14(write_en14), .out15(write_en15),
    .out16(write_en16), .out17(write_en17), .out18(write_en18), .out19(write_en19), .out20(write_en20),
    .out21(write_en21), .out22(write_en22), .out23(write_en23), .out24(write_en24), .out25(write_en25),
    .out26(write_en26), .out27(write_en27), .out28(write_en28), .out29(write_en29), .out30(write_en30),
    .out31(write_en31), .sel(rd), .en(RegWEn));  // open: out0
  Register #(.width(32), .trigger("rising"), .Select("low")) register_20 (
    .D(Write_Data), .en(write_en5), .Q(t0), .clk(clk));  // open: clr
  Register #(.width(32), .trigger("rising"), .Select("low")) register_21 (
    .D(Write_Data), .en(write_en13), .Q(x13), .clk(clk));  // open: clr
  Register #(.width(32), .trigger("rising"), .Select("low")) register_22 (
    .D(Write_Data), .en(write_en21), .Q(x21), .clk(clk));  // open: clr
  Register #(.width(32), .trigger("rising"), .Select("low")) register_23 (
    .D(Write_Data), .en(write_en29), .Q(x29), .clk(clk));  // open: clr
  Pull_Resistor #(.pull(0)) pull_resistor_24 (.node(write_en24));
  // Probe on rd
  Pull_Resistor #(.pull(0)) pull_resistor_25 (.node(write_en25));
  Pull_Resistor #(.pull(0)) pull_resistor_26 (.node(write_en26));
  Pull_Resistor #(.pull(0)) pull_resistor_27 (.node(write_en27));
  Pull_Resistor #(.pull(0)) pull_resistor_28 (.node(write_en28));
  Register #(.width(32), .trigger("rising"), .Select("low")) register_24 (
    .D(Write_Data), .en(write_en6), .Q(t1), .clk(clk));  // open: clr
  Register #(.width(32), .trigger("rising"), .Select("low")) register_25 (
    .D(Write_Data), .en(write_en14), .Q(x14), .clk(clk));  // open: clr
  Register #(.width(32), .trigger("rising"), .Select("low")) register_26 (
    .D(Write_Data), .en(write_en22), .Q(x22), .clk(clk));  // open: clr
  Register #(.width(32), .trigger("rising"), .Select("low")) register_27 (
    .D(Write_Data), .en(write_en30), .Q(x30), .clk(clk));  // open: clr
  // Probe on x30
  Pull_Resistor #(.pull(0)) pull_resistor_29 (.node(write_en29));
  Pull_Resistor #(.pull(0)) pull_resistor_30 (.node(write_en30));
  Pull_Resistor #(.pull(0)) pull_resistor_31 (.node(write_en31));
  // Probe on Read_Data_1
  // Probe on rs1
  Register #(.width(32), .trigger("rising"), .Select("low")) register_28 (
    .D(Write_Data), .en(write_en7), .Q(t2), .clk(clk));  // open: clr
  Register #(.width(32), .trigger("rising"), .Select("low")) register_29 (
    .D(Write_Data), .en(write_en15), .Q(x15), .clk(clk));  // open: clr
  Register #(.width(32), .trigger("rising"), .Select("low")) register_30 (
    .D(Write_Data), .en(write_en23), .Q(x23), .clk(clk));  // open: clr
  Register #(.width(32), .trigger("rising"), .Select("low")) register_31 (
    .D(Write_Data), .en(write_en31), .Q(x31), .clk(clk));  // open: clr
  Multiplexer #(.select(5), .width(32), .disabled("Z"), .enable("false")) multiplexer_1 (
    .in0({32{1'b0}}), .in1(ra), .in2(sp), .in3(x3), .in4(x4), .in5(t0), .in6(t1), .in7(t2), .in8(s0),
    .in9(s1), .in10(a0), .in11(x11), .in12(x12), .in13(x13), .in14(x14), .in15(x15), .in16(x16), .in17(x17),
    .in18(x18), .in19(x19), .in20(x20), .in21(x21), .in22(x22), .in23(x23), .in24(x24), .in25(x25),
    .in26(x26), .in27(x27), .in28(x28), .in29(x29), .in30(x30), .in31(x31), .out(Read_Data_1), .sel(rs1));
  // Probe on Read_Data_2
  // Probe on rs2
  Multiplexer #(.select(5), .width(32), .disabled("Z"), .enable("false")) multiplexer_2 (
    .in0({32{1'b0}}), .in1(ra), .in2(sp), .in3(x3), .in4(x4), .in5(t0), .in6(t1), .in7(t2), .in8(s0),
    .in9(s1), .in10(a0), .in11(x11), .in12(x12), .in13(x13), .in14(x14), .in15(x15), .in16(x16), .in17(x17),
    .in18(x18), .in19(x19), .in20(x20), .in21(x21), .in22(x22), .in23(x23), .in24(x24), .in25(x25),
    .in26(x26), .in27(x27), .in28(x28), .in29(x29), .in30(x30), .in31(x31), .out(Read_Data_2), .sel(rs2));

  // Other names for the same wires on the sheet: read_data1[31:0] = Read_Data_1; read_data2[31:0] = Read_Data_2;
  //   read_reg1[4:0] = rs1; read_reg2[4:0] = rs2; write_en = RegWEn; write_reg[4:0] = rd; x1[31:0] = ra;
  //   x2[31:0] = sp; x5[31:0] = t0; x6[31:0] = t1; x7[31:0] = t2; x8[31:0] = s0; x9[31:0] = s1; x10[31:0] = a0

  // Notes on the sheet:
  //   INPUTS to your circuit
  //   DON'T CHANGE THE LOCATIONS OF THE INPUTS AND OUTPUTS!
  //   These are DEBUG/TEST outputs from your circuit.
  //   OUTPUTS from your circuit
endmodule

module ControlModel (
  input  [31:0] Instruction,
  output BrUN,
  output RegWrite,
  output MemWrite,
  output MemRead,
  output PCSel,
  output [2:0] ImmSel,
  output ALUSelA,
  output ALUSelB,
  output [1:0] WBSel,
  output [3:0] ALUOP,
  output BEQ,
  output BLT,
  output BNE,
  output BLTU,
  output BGE,
  output BGEU
);

  wire and_5_out, and_10_out, comparator_3_eq, comparator_4_eq, comparator_5_eq, comparator_6_eq,
       comparator_7_eq, comparator_8_eq, comparator_13_eq, comparator_14_eq, comparator_15_eq,
       comparator_16_eq, comparator_17_eq, comparator_18_eq, comparator_19_eq, comparator_20_eq, IType, JALR,
       Load, or_2_out, or_3_out, or_4_out, or_5_out, or_11_out, or_12_out, RType, SBType, UJType, UType;
  wire [1:0] priority_encoder_4_out;
  wire [2:0] priority_encoder_3_out;
  wire [3:0] AOP_I, AOP_R, rom_2_data;

  Comparator #(.width(7), .mode("unsigned")) comparator_1 (
    .a(Instruction[6:0]), .b(7'b0110011), .eq(RType));  // open: gt, lt
  Comparator #(.width(7), .mode("unsigned")) comparator_2 (
    .a(Instruction[6:0]), .b(7'b0000011), .eq(MemRead));  // open: gt, lt
  Comparator #(.width(7), .mode("unsigned")) comparator_3 (
    .a(Instruction[6:0]), .b(7'b1100111), .eq(comparator_3_eq));  // open: gt, lt
  Comparator #(.width(7), .mode("unsigned")) comparator_4 (
    .a(Instruction[6:0]), .b(7'b0010011), .eq(comparator_4_eq));  // open: gt, lt
  Comparator #(.width(7), .mode("unsigned")) comparator_5 (
    .a(Instruction[6:0]), .b(7'b0000011), .eq(comparator_5_eq));  // open: gt, lt
  and and_1 (Load, comparator_5_eq, IType);
  Comparator #(.width(3), .mode("unsigned")) comparator_6 (
    .a(Instruction[14:12]), .b(3'b000), .eq(comparator_6_eq));  // open: gt, lt
  Comparator #(.width(3), .mode("unsigned")) comparator_7 (
    .a(Instruction[14:12]), .b(3'b001), .eq(comparator_7_eq));  // open: gt, lt
  Comparator #(.width(3), .mode("unsigned")) comparator_8 (
    .a(Instruction[14:12]), .b(3'b101), .eq(comparator_8_eq));  // open: gt, lt
  or or_1 (IType, MemRead, comparator_3_eq, comparator_4_eq);
  and and_2 (BEQ, comparator_6_eq, SBType);
  and and_3 (BNE, comparator_7_eq, SBType);
  and and_4 (BGE, comparator_8_eq, SBType);
  and and_5 (and_5_out, IType, ~JALR);  // AND_Gate
  Comparator #(.width(7), .mode("unsigned")) comparator_9 (
    .a(Instruction[6:0]), .b(7'b0110111), .eq(UType));  // open: gt, lt
  Comparator #(.width(7), .mode("unsigned")) comparator_10 (
    .a(Instruction[6:0]), .b(7'b1101111), .eq(UJType));  // open: gt, lt
  Comparator #(.width(7), .mode("unsigned")) comparator_11 (
    .a(Instruction[6:0]), .b(7'b0100011), .eq(MemWrite));  // open: gt, lt
  Comparator #(.width(7), .mode("unsigned")) comparator_12 (
    .a(Instruction[6:0]), .b(7'b1100011), .eq(SBType));  // open: gt, lt
  Comparator #(.width(7), .mode("unsigned")) comparator_13 (
    .a(Instruction[6:0]), .b(7'b1100111), .eq(comparator_13_eq));  // open: gt, lt
  Comparator #(.width(3), .mode("unsigned")) comparator_14 (
    .a(Instruction[14:12]), .b(3'b100), .eq(comparator_14_eq));  // open: gt, lt
  Comparator #(.width(3), .mode("unsigned")) comparator_15 (
    .a(Instruction[14:12]), .b(3'b110), .eq(comparator_15_eq));  // open: gt, lt
  Comparator #(.width(3), .mode("unsigned")) comparator_16 (
    .a(Instruction[14:12]), .b(3'b111), .eq(comparator_16_eq));  // open: gt, lt
  and and_6 (JALR, comparator_13_eq, IType);
  or or_2 (or_2_out, RType, and_5_out, UType);
  and and_7 (BLT, comparator_14_eq, SBType);
  and and_8 (BLTU, comparator_15_eq, SBType);
  and and_9 (BGEU, comparator_16_eq, SBType);
  or or_3 (or_3_out, UJType, JALR);
  or or_4 (or_4_out, or_3_out, or_2_out, Load);
  Priority_Encoder #(.select(3), .disabled("Z")) priority_encoder_1 (
    .in0(IType), .in1(MemWrite), .in2(SBType), .in3(UType), .in4(UJType), .out(ImmSel), .en_in(or_5_out));  // open: in5, in6, in7, gs, en_out
  or or_5 (or_5_out, IType, MemWrite, SBType, UType, UJType);
  Priority_Encoder #(.select(2), .disabled("Z")) priority_encoder_2 (
    .in0(or_3_out), .in1(or_2_out), .in2(Load), .out(WBSel), .en_in(or_4_out));  // open: in3, gs, en_out
  Pull_Resistor #(.pull(0)) pull_resistor_1 (.node(WBSel));
  or or_6 (BrUN, BLTU, BGEU);
  or or_7 (RegWrite, RType, IType, UType, UJType);
  or or_8 (PCSel, JALR, UJType);
  Pull_Resistor #(.pull(0)) pull_resistor_2 (.node(ImmSel));
  or or_9 (ALUSelA, SBType, UJType);
  or or_10 (ALUSelB, IType, MemWrite, SBType, UType, UJType);
  // Probe on PCSel
  // Probe on Instruction[6:0]
  Comparator #(.width(7), .mode("unsigned")) comparator_17 (
    .a(7'b0010011), .b(Instruction[6:0]), .eq(comparator_17_eq));  // open: gt, lt
  Comparator #(.width(3), .mode("unsigned")) comparator_18 (
    .a(3'b101), .b(Instruction[14:12]), .eq(comparator_18_eq));  // open: gt, lt
  Comparator #(.width(7), .mode("unsigned")) comparator_19 (
    .a(7'b0100000), .b(Instruction[31:25]), .eq(comparator_19_eq));  // open: gt, lt
  Comparator #(.width(7), .mode("unsigned")) comparator_20 (
    .a(7'b0000011), .b(Instruction[6:0]), .eq(comparator_20_eq));  // open: gt, lt
  // Probe on comparator_20_eq
  ROM #(.addrWidth(10), .dataWidth(4), .Select("high")) rom_1 (
    .addr({Instruction[14:12], Instruction[31:25]}), .data(AOP_R));
  ROM #(.addrWidth(3), .dataWidth(4), .Select("high")) rom_2 (.addr(Instruction[14:12]), .data(rom_2_data));
  // Probe on and_10_out
  and and_10 (and_10_out, comparator_17_eq, comparator_18_eq, comparator_19_eq);
  or or_11 (or_11_out, and_10_out, comparator_20_eq);
  Priority_Encoder #(.select(3), .disabled("Z")) priority_encoder_3 (
    .in0(RType), .in1(IType), .in2(MemWrite), .in3(SBType), .in4(UType), .in5(UJType),
    .out(priority_encoder_3_out), .en_in(or_12_out));  // open: in6, in7, gs, en_out
  or or_12 (or_12_out, RType, IType, MemWrite, SBType, UType, UJType);
  Priority_Encoder #(.select(2), .disabled("Z")) priority_encoder_4 (
    .in1(and_10_out), .in2(comparator_20_eq), .out(priority_encoder_4_out), .en_in(or_11_out));  // open: in0, in3, gs, en_out
  // Probe on or_11_out
  Pull_Resistor #(.pull(0)) pull_resistor_3 (.node(priority_encoder_3_out));
  // Probe on AOP_I
  Multiplexer #(.select(2), .width(4), .disabled("Z"), .enable("false")) multiplexer_1 (
    .in0(rom_2_data), .in1(4'b0101), .in2(4'b0000), .out(AOP_I), .sel(priority_encoder_4_out));  // open: in3
  Pull_Resistor #(.pull(0)) pull_resistor_4 (.node(priority_encoder_4_out));
  // Probe on priority_encoder_3_out
  // Probe on priority_encoder_4_out
  Multiplexer #(.select(3), .width(4), .disabled("Z"), .enable("false")) multiplexer_2 (
    .in0(AOP_R), .in1(AOP_I), .in2(4'b0000), .in3(4'b0000), .in4(4'b1101), .in5(4'b0000), .out(ALUOP),
    .sel(priority_encoder_3_out));  // open: in6, in7
  // Probe on ALUOP

  // Other names for the same wires on the sheet: Funct7[6:0] = Instruction[31:25]; Funct3[2:0] = Instruction[14:12];
  //   AOP[3:0] = ALUOP; OPCODE[6:0] = Instruction[6:0]; SType = MemWrite

  // Notes on the sheet:
  //   Extract the filed in Instrutions
  //   contents of rom_1 (hex, n*v repeats v):
  //   0 a c 12*0 f 16*0 c 95*0 6 e 126*0 7 128*0 b 126*0 3 127*0 4 8 126*0 2 127*0 1 9
  //   contents of rom_2 (hex, n*v repeats v):
  //   0 6 7 7 3 4 2 1
endmodule

module AluModel (
  input  [31:0] A,
  input  [31:0] B,
  input  [3:0] ALUSel,
  output [31:0] Result
);

  wire adder_3_cout, bitselector_1_out, bitselector_2_out, xor_1_out;
  wire [0:0] slt_alu;
  wire [15:0] adder_5_out, undriven, undriven_2;
  wire [31:0] add, adder_1_out, adder_3_out, and_alu, divu_alu, mul_alu, mulh_alu, mulhu_alu,
       multiplexer_1_out, multiplexer_2_out, multiplier_1_cout, multiplier_1_out, negator_1_out,
       negator_2_out, not_1_out, not_2_out, or_alu, remu_alu, sll_alu, sra_alu, srl_alu, sub_alu, xor_alu;
  wire [31:16] vaddh_alu;

  BitSelector #(.width(32), .group(1)) bitselector_1 (.in(A), .out(bitselector_1_out), .sel({5{1'b1}}));
  BitSelector #(.width(32), .group(1)) bitselector_2 (.in(B), .out(bitselector_2_out), .sel({5{1'b1}}));
  Negator #(.width(32)) negator_1 (.in(A), .out(negator_1_out));
  Negator #(.width(32)) negator_2 (.in(B), .out(negator_2_out));
  Multiplexer #(.select(1), .width(32), .disabled("Z"), .enable("false")) multiplexer_1 (
    .in0(A), .in1(negator_1_out), .out(multiplexer_1_out), .sel(bitselector_1_out));
  Multiplexer #(.select(1), .width(32), .disabled("Z"), .enable("false")) multiplexer_2 (
    .in0(B), .in1(negator_2_out), .out(multiplexer_2_out), .sel(bitselector_2_out));
  Multiplier #(.width(32)) multiplier_1 (
    .a(multiplexer_1_out), .b(multiplexer_2_out), .out(multiplier_1_out), .cout(multiplier_1_cout));  // open: cin
  xor xor_1 (xor_1_out, bitselector_1_out, bitselector_2_out);
  assign not_1_out = ~multiplier_1_out;  // NOT_Gate not_1, 32 bits wide
  Adder #(.width(32)) adder_1 (.a({32{1'b0}}), .b(not_2_out), .out(adder_1_out), .cin(adder_3_cout));  // open: cout
  assign not_2_out = ~multiplier_1_cout;  // NOT_Gate not_2, 32 bits wide
  Adder #(.width(32)) adder_2 (.a(A), .b(B), .out(add));  // open: cin, cout
  assign and_alu = A & B;  // AND_Gate and_1, 32 bits wide
  assign or_alu = A | B;  // OR_Gate or_1, 32 bits wide
  assign xor_alu = A ^ B;  // XOR_Gate xor_2, 32 bits wide
  Shifter #(.width(32), .shift("lr")) shifter_1 (.in(A), .\dist (B[4:0]), .out(srl_alu));
  Shifter #(.width(32), .shift("ar")) shifter_2 (.in(A), .\dist (B[4:0]), .out(sra_alu));
  Shifter #(.width(32), .shift("ll")) shifter_3 (.in(A), .\dist (B[4:0]), .out(sll_alu));
  Comparator #(.width(32), .mode("twosComplement")) comparator_1 (.a(A), .b(B), .lt(slt_alu[0]));  // open: gt, eq
  Adder #(.width(32)) adder_3 (.a(32'h1), .b(not_1_out), .out(adder_3_out), .cout(adder_3_cout));  // open: cin
  Multiplexer #(.select(1), .width(32), .disabled("Z"), .enable("false")) multiplexer_3 (
    .in0(multiplier_1_out), .in1(adder_3_out), .out(mul_alu), .sel(xor_1_out));
  Multiplexer #(.select(1), .width(32), .disabled("Z"), .enable("false")) multiplexer_4 (
    .in0(multiplier_1_cout), .in1(adder_1_out), .out(mulh_alu), .sel(xor_1_out));
  Divider #(.width(32)) divider_1 (.a(A), .b(B), .out(divu_alu), .rem(remu_alu));  // open: upper
  Multiplier #(.width(32)) multiplier_2 (.a(A), .b(B), .cout(mulhu_alu));  // open: out, cin
  Subtractor #(.width(32)) subtractor_1 (.a(A), .b(B), .out(sub_alu));  // open: bin, bout
  // Probe on Result
  Multiplexer #(.select(4), .width(32), .disabled("Z"), .enable("false")) multiplexer_5 (
    .in0(add), .in1(and_alu), .in2(or_alu), .in3(xor_alu), .in4(srl_alu), .in5(sra_alu), .in6(sll_alu),
    .in7({{31{1'b0}}, slt_alu[0]}), .in8(divu_alu), .in9(remu_alu), .in10(mul_alu), .in11(mulhu_alu),
    .in12(sub_alu), .in13(B), .in14(mulh_alu), .in15({vaddh_alu, vaddh_alu}), .out(Result), .sel(ALUSel));
  Adder #(.width(16)) adder_4 (.a(A[31:16]), .b(B[31:16]), .out(vaddh_alu));  // open: cin, cout
  Adder #(.width(16)) adder_5 (.a(undriven), .b(undriven_2), .out(adder_5_out));  // open: cin, cout

  // Other names for the same wires on the sheet: vaddh_alu[15:0] = vaddh_alu

  // Notes on the sheet:
  //   INPUTS to your circuit
  //   DON'T CHANGE THE LOCATIONS OF THE INPUTS AND OUTPUTS!
  //   OUTPUT from your circuit
endmodule

module ImmModel (
  input  [31:0] INSTRUCTION,
  input  [2:0] InstructionType,
  output [31:0] Immdiate
);

  wire [31:0] bit_extender_1_out, bit_extender_2_out, bit_extender_3_out, bit_extender_4_out;

  // Probe on INSTRUCTION
  assign bit_extender_1_out = {{20{INSTRUCTION[31]}}, INSTRUCTION[31:20]};  // Bit_Extender bit_extender_1
  assign bit_extender_2_out = {{20{INSTRUCTION[31]}}, {INSTRUCTION[31:25], INSTRUCTION[11:7]}};  // Bit_Extender bit_extender_2
  assign bit_extender_3_out = {{19{INSTRUCTION[31]}}, {INSTRUCTION[31], INSTRUCTION[7], INSTRUCTION[30:25], INSTRUCTION[11:8], 1'b0}};  // Bit_Extender bit_extender_3
  // Probe on bit_extender_3_out
  assign bit_extender_4_out = {{11{INSTRUCTION[31]}}, {INSTRUCTION[31], INSTRUCTION[19:12], INSTRUCTION[20], INSTRUCTION[30:21], 1'b0}};  // Bit_Extender bit_extender_4
  Multiplexer #(.select(3), .width(32), .disabled("Z"), .enable("false")) multiplexer_1 (
    .in0(bit_extender_1_out), .in1(bit_extender_2_out), .in2(bit_extender_3_out),
    .in3({INSTRUCTION[31:12], {12{1'b0}}}), .in4(bit_extender_4_out), .out(Immdiate), .sel(InstructionType));  // open: in5, in6, in7

  // Notes on the sheet:
  //   I
  //   S
  //   U
  //   SB
  //   UJ
endmodule

module Branch (
  input  [31:0] RS1,
  input  [31:0] RS2,
  input  BrUN,
  output BrEQ,
  output BrLT
);

  wire comparator_1_lt, comparator_2_lt;

  Comparator #(.width(32), .mode("twosComplement")) comparator_1 (
    .a(RS1), .b(RS2), .eq(BrEQ), .lt(comparator_1_lt));  // open: gt
  Comparator #(.width(32), .mode("unsigned")) comparator_2 (.a(RS1), .b(RS2), .lt(comparator_2_lt));  // open: gt, eq
  Multiplexer #(.select(1), .width(1), .disabled("Z"), .enable("false")) multiplexer_1 (
    .in0(comparator_1_lt), .in1(comparator_2_lt), .out(BrLT), .sel(BrUN));
endmodule

module IMEM (
  input  [31:0] Program_counter,
  output [31:0] Instruction
);

  ROM #(.addrWidth(16), .dataWidth(32), .Select("high")) rom_1 (.addr(Program_counter[17:2]), .data(Instruction));

  // Notes on the sheet:
  //   contents of rom_1 (hex, n*v repeats v):
  //   fffff437 204e493 2296913 c0006f 493 913 663 493 913 1201663 493 913 1c000ef a00913 13 13 204e493 13
  //   13 fff48493 13 13 942023 13 13 fe0494e3 8067
endmodule

module DMEM (
  input  [31:0] Write_Data,
  input  clk,
  input  Read_En,
  input  [31:0] Address,
  input  Write_En,
  output [15:0] MissNubmer,
  output [31:0] Read_Data
);

  wire and_1_out, and_2_out, and_3_out, and_4_out, is_MemAddr, is_RomAddr, or_1_out;
  wire [15:0] controlled_buffer_3_out;
  wire [31:0] controlled_buffer_1_out, controlled_buffer_2_out, ram_1_data, rom_1_data;

  or or_1 (or_1_out, Read_En, Write_En);
  and and_1 (and_1_out, or_1_out, is_MemAddr);
  assign controlled_buffer_1_out = and_1_out ? Address : 32'bz;  // Controlled_Buffer controlled_buffer_1
  Comparator #(.width(4), .mode("unsigned")) comparator_1 (
    .a(Address[31:28]), .b(4'b1000), .eq(is_RomAddr));  // open: gt, lt
  assign controlled_buffer_2_out = and_2_out ? Write_Data : 32'bz;  // Controlled_Buffer controlled_buffer_2
  and and_2 (and_2_out, is_MemAddr, Write_En);
  assign controlled_buffer_3_out = is_RomAddr ? Address[17:2] : 16'bz;  // Controlled_Buffer controlled_buffer_3
  not not_1 (is_MemAddr, is_RomAddr);
  RAM #(.addrWidth(16), .dataWidth(32), .bus("separate"), .Select("high")) ram_1 (
    .addr(controlled_buffer_1_out[17:2]), .din(controlled_buffer_2_out), .data(ram_1_data), .str(and_2_out),
    .clk(clk), .ld(1'b1));  // open: sel, clr
  ROM #(.addrWidth(16), .dataWidth(32), .Select("high")) rom_1 (.addr(controlled_buffer_3_out), .data(rom_1_data));
  and and_3 (and_3_out, Read_En, is_MemAddr);
  assign Read_Data = and_3_out ? ram_1_data : 32'bz;  // Controlled_Buffer controlled_buffer_4
  assign Read_Data = and_4_out ? rom_1_data : 32'bz;  // Controlled_Buffer controlled_buffer_5
  and and_4 (and_4_out, Read_En, is_RomAddr);

  // Other names for the same wires on the sheet: Addr[31:0] = Address; MissNumber[15:0] = MissNubmer;
  //   ReadData[31:0] = Read_Data; ReadEnable = Read_En; WriteData[31:0] = Write_Data; WriteEnable = Write_En

  // Notes on the sheet:
  //   输入引脚区
  //   二级存储器
  //   contents of rom_1 (hex, n*v repeats v):
  //   0 1 2 3 4 5 6 7 8 9 a b c d e f 10 11 12 13 14 15 16 17 18 19 1a 1b 1c 1d 1e 1f 20 21 22 23 24 25 26
  //   27 28 29 2a 2b 2c 2d 2e 2f 30 31 32 33 34 35 36 37 38 39 3a 3b 3c 3d 3e 3f 40 41 42 43 44 45 46 47
  //   48 49 4a 4b 4c 4d 4e 4f 50 51 52 53 54 55 56 57 58 59 5a 5b 5c 5d 5e 5f 60 61 62 63 64 65 66 67 68
  //   69 6a 6b 6c 6d 6e 6f 70 71 72 73 74 75 76 77 78 79 7a 7b 7c 7d 7e 7f ffffff80 ffffff81 ffffff82
  //   ffffff83 ffffff84 ffffff85 ffffff86 ffffff87 ffffff88 ffffff89 ffffff8a ffffff8b ffffff8c ffffff8d
  //   ffffff8e ffffff8f ffffff90 ffffff91 ffffff92 ffffff93 ffffff94 ffffff95 ffffff96 ffffff97 ffffff98
  //   ffffff99 ffffff9a ffffff9b ffffff9c ffffff9d ffffff9e ffffff9f ffffffa0 ffffffa1 ffffffa2 ffffffa3
  //   ffffffa4 ffffffa5 ffffffa6 ffffffa7 ffffffa8 ffffffa9 ffffffaa ffffffab ffffffac ffffffad ffffffae
  //   ffffffaf ffffffb0 ffffffb1 ffffffb2 ffffffb3 ffffffb4 ffffffb5 ffffffb6 ffffffb7 ffffffb8 ffffffb9
  //   ffffffba ffffffbb ffffffbc ffffffbd ffffffbe ffffffbf ffffffc0 ffffffc1 ffffffc2 ffffffc3 ffffffc4
  //   ffffffc5 ffffffc6 ffffffc7 ffffffc8 ffffffc9 ffffffca ffffffcb ffffffcc ffffffcd ffffffce ffffffcf
  //   ffffffd0 ffffffd1 ffffffd2 ffffffd3 ffffffd4 ffffffd5 ffffffd6 ffffffd7 ffffffd8 ffffffd9 ffffffda
  //   ffffffdb ffffffdc ffffffdd ffffffde ffffffdf ffffffe0 ffffffe1 ffffffe2 ffffffe3 ffffffe4 ffffffe5
  //   ffffffe6 ffffffe7 ffffffe8 ffffffe9 ffffffea ffffffeb ffffffec ffffffed ffffffee ffffffef fffffff0
  //   fffffff1 fffffff2 fffffff3 fffffff4 fffffff5 fffffff6 fffffff7 fffffff8 fffffff9 fffffffa fffffffb
  //   fffffffc fffffffd fffffffe ffffffff 0 1 2 3 4 5 6 7 8 9 a b c d e f 10 11 12 13 14 15 16 17 18 19 1a
  //   1b 1c 1d 1e 1f 20 21 22 23 24 25 26 27 28 29 2a 2b 2c 2d 2e 2f 30 31 32 33 34 35 36 37 38 39 3a 3b
  //   3c 3d 3e 3f 40 41 42 43 44 45 46 47 48 49 4a 4b 4c 4d 4e 4f 50 51 52 53 54 55 56 57 58 59 5a 5b 5c
  //   5d 5e 5f 60 61 62 63 64 65 66 67 68 69 6a 6b 6c 6d 6e 6f 70 71 72 73 74 75 76 77 78 79 7a 7b 7c 7d
  //   7e 7f ffffff80 ffffff81 ffffff82 ffffff83 ffffff84 ffffff85 ffffff86 ffffff87 ffffff88 ffffff89
  //   ffffff8a ffffff8b ffffff8c ffffff8d ffffff8e ffffff8f ffffff90 ffffff91 ffffff92 ffffff93 ffffff94
  //   ffffff95 ffffff96 ffffff97 ffffff98 ffffff99 ffffff9a ffffff9b ffffff9c ffffff9d ffffff9e ffffff9f
  //   ffffffa0 ffffffa1 ffffffa2 ffffffa3 ffffffa4 ffffffa5 ffffffa6 ffffffa7 ffffffa8 ffffffa9 ffffffaa
  //   ffffffab ffffffac ffffffad ffffffae ffffffaf ffffffb0 ffffffb1 ffffffb2 ffffffb3 ffffffb4 ffffffb5
  //   ffffffb6 ffffffb7 ffffffb8 ffffffb9 ffffffba ffffffbb ffffffbc ffffffbd ffffffbe ffffffbf ffffffc0
  //   ffffffc1 ffffffc2 ffffffc3 ffffffc4 ffffffc5 ffffffc6 ffffffc7 ffffffc8 ffffffc9 ffffffca ffffffcb
  //   ffffffcc ffffffcd ffffffce ffffffcf ffffffd0 ffffffd1 ffffffd2 ffffffd3 ffffffd4 ffffffd5 ffffffd6
  //   ffffffd7 ffffffd8 ffffffd9 ffffffda ffffffdb ffffffdc ffffffdd ffffffde ffffffdf ffffffe0 ffffffe1
  //   ffffffe2 ffffffe3 ffffffe4 ffffffe5 ffffffe6 ffffffe7 ffffffe8 ffffffe9 ffffffea ffffffeb ffffffec
  //   ffffffed ffffffee ffffffef fffffff0 fffffff1 fffffff2 fffffff3 fffffff4 fffffff5 fffffff6 fffffff7
  //   fffffff8 fffffff9 fffffffa fffffffb fffffffc fffffffd fffffffe ffffffff 0 1 2 3 4 5 6 7 8 9 a b c d
  //   e f 10 11 12 13 14 15 16 17 18 19 1a 1b 1c 1d 1e 1f 20 21 22 23 24 25 26 27 28 29 2a 2b 2c 2d 2e 2f
  //   30 31 32 33 34 35 36 37 38 39 3a 3b 3c 3d 3e 3f 40 41 42 43 44 45 46 47 48 49 4a 4b 4c 4d 4e 4f 50
  //   51 52 53 54 55 56 57 58 59 5a 5b 5c 5d 5e 5f 60 61 62 63 64 65 66 67 68 69 6a 6b 6c 6d 6e 6f 70 71
  //   72 73 74 75 76 77 78 79 7a 7b 7c 7d 7e 7f ffffff80 ffffff81 ffffff82 ffffff83 ffffff84 ffffff85
  //   ffffff86 ffffff87 ffffff88 ffffff89 ffffff8a ffffff8b ffffff8c ffffff8d ffffff8e ffffff8f ffffff90
  //   ffffff91 ffffff92 ffffff93 ffffff94 ffffff95 ffffff96 ffffff97 ffffff98 ffffff99 ffffff9a ffffff9b
  //   ffffff9c ffffff9d ffffff9e ffffff9f ffffffa0 ffffffa1 ffffffa2 ffffffa3 ffffffa4 ffffffa5 ffffffa6
  //   ffffffa7 ffffffa8 ffffffa9 ffffffaa ffffffab ffffffac ffffffad ffffffae ffffffaf ffffffb0 ffffffb1
  //   ffffffb2 ffffffb3 ffffffb4 ffffffb5 ffffffb6 ffffffb7 ffffffb8 ffffffb9 ffffffba ffffffbb ffffffbc
  //   ffffffbd ffffffbe ffffffbf ffffffc0 ffffffc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
  //   输出引脚区
endmodule

module BusModel (
  input  [31:0] WriteAddr,
  input  [31:0] WriteData,
  input  R,
  input  W,
  input  [31:0] IORead,
  input  [31:0] MemRead,
  output [31:0] ReadData,
  output out_8,
  output IOEn,
  output [11:0] IOAddr12,
  output [31:0] IOWriteData,
  output [31:0] MemAddr,
  output MemR,
  output MemW,
  output [31:0] MemWriteData
);

  wire and_1_out, and_2_out, and_3_out, and_4_out, is_MemAddr, or_1_out;

  // Probe on WriteAddr
  assign MemW = is_MemAddr ? W : 1'bz;  // Controlled_Buffer controlled_buffer_1
  Comparator #(.width(20), .mode("unsigned")) comparator_1 (
    .a(WriteAddr[31:12]), .b({20{1'b1}}), .eq(IOEn));  // open: gt, lt
  assign MemR = is_MemAddr ? R : 1'bz;  // Controlled_Buffer controlled_buffer_2
  // Probe on IOEn
  not not_1 (is_MemAddr, IOEn);
  or or_1 (or_1_out, R, W);
  and and_1 (and_1_out, is_MemAddr, or_1_out);
  // Probe on WriteAddr
  assign MemAddr = and_1_out ? WriteAddr : 32'bz;  // Controlled_Buffer controlled_buffer_3
  // Probe on MemAddr
  and and_2 (and_2_out, is_MemAddr, W);
  assign MemWriteData = and_2_out ? WriteData : 32'bz;  // Controlled_Buffer controlled_buffer_4
  and and_3 (and_3_out, R, IOEn);
  assign ReadData = and_3_out ? IORead : 32'bz;  // Controlled_Buffer controlled_buffer_5
  assign ReadData = and_4_out ? MemRead : 32'bz;  // Controlled_Buffer controlled_buffer_6
  and and_4 (and_4_out, R, is_MemAddr);
  // Probe on ReadData

  assign IOAddr12 = WriteAddr[11:0];
  assign IOWriteData = WriteData;

  // Other names for the same wires on the sheet: IORW = out_8; RW = out_8
endmodule

module LedDriver (
  input  IOEn,
  input  [11:0] IOAddr12,
  input  [31:0] IOWriteData,
  input  in_4,
  output [31:0] DisplayData
);

  wire and_1_out, comparator_1_eq;
  wire [31:0] multiplexer_1_out;

  Comparator #(.width(12), .mode("unsigned")) comparator_1 (
    .a({12{1'b0}}), .b(IOAddr12), .eq(comparator_1_eq));  // open: gt, lt
  and and_1 (and_1_out, comparator_1_eq, IOEn);
  Multiplexer #(.select(1), .width(32), .disabled("Z"), .enable("false")) multiplexer_1 (
    .in1(IOWriteData), .out(multiplexer_1_out), .sel(and_1_out));  // open: in0
  Register #(.width(32), .trigger("rising"), .Select("low")) register_1 (
    .D(multiplexer_1_out), .en(and_1_out), .Q(DisplayData), .clk(in_4));  // open: clr

  // Other names for the same wires on the sheet: clk = in_4
endmodule

module KeyTTYDriver (
  input  IOEn,
  input  in_2,
  input  [11:0] IOAddr12,
  input  [31:0] IOWriteData,
  input  clk,
  input  [6:0] KeyValue,
  input  KeyEn,
  output clock,
  output [31:0] IORead,
  output [6:0] TTYData,
  output TTYEnable
);

  wire and_1_out, comparator_1_eq, comparator_2_eq;

  Comparator #(.width(12), .mode("unsigned")) comparator_1 (
    .a(12'h4), .b(IOAddr12), .eq(comparator_1_eq));  // open: gt, lt
  Comparator #(.width(12), .mode("unsigned")) comparator_2 (
    .a(12'h8), .b(IOAddr12), .eq(comparator_2_eq));  // open: gt, lt
  and and_1 (and_1_out, comparator_1_eq, IOEn);
  and and_2 (TTYEnable, comparator_2_eq, IOEn);
  // Probe on IOEn
  // Probe on IOWriteData
  Multiplexer #(.select(1), .width(32), .disabled("Z"), .enable("false")) multiplexer_1 (
    .in1({KeyEn, {24{1'b0}}, KeyValue}), .out(IORead), .sel(and_1_out));  // open: in0
  Multiplexer #(.select(1), .width(7), .disabled("Z"), .enable("false")) multiplexer_2 (
    .in1(IOWriteData[6:0]), .out(TTYData), .sel(TTYEnable));  // open: in0
  // Probe on IORead

  assign clock = clk;

  // Other names for the same wires on the sheet: IORW = in_2
endmodule

module DMEMCache (
  input  [31:0] Write_Data,
  input  clk,
  input  Read_En,
  input  [31:0] Address,
  input  Write_En,
  output Miss,
  output [15:0] MissNubmer,
  output [31:0] Read_Data
);

  wire and_1_out, and_2_out, and_3_out, and_4_out, and_5_out, \cache直接相联_1_miss , is_MemAddr, is_RomAddr,
       or_1_out, RDY;
  wire [15:0] controlled_buffer_4_out, controlled_buffer_6_out, counter_1_q, ExChangeAddr;
  wire [31:0] \cache直接相联_1_dataout , controlled_buffer_1_out, controlled_buffer_5_out,
       exchange_logic_1_blockdatain0, exchange_logic_1_blockdatain1, exchange_logic_1_blockdatain2,
       exchange_logic_1_blockdatain3, ExChangeData, RAM_data, rom_1_data;

  assign controlled_buffer_1_out = Read_En ? Address : 32'bz;  // Controlled_Buffer controlled_buffer_1
  Pull_Resistor #(.pull(0)) pull_resistor_1 (.node(controlled_buffer_1_out));
  Comparator #(.width(4), .mode("unsigned")) comparator_1 (
    .a(Address[31:28]), .b(4'b1000), .eq(is_RomAddr));  // open: gt, lt
  not not_1 (is_MemAddr, is_RomAddr);
  assign Read_Data = Read_En ? \cache直接相联_1_dataout  : 32'bz;  // Controlled_Buffer controlled_buffer_2
  \Cache直接相联  \cache直接相联_1  (
    .BlockDataIn(exchange_logic_1_blockdatain0), .Addr(controlled_buffer_1_out[17:2]), .BlkDataReady(RDY),
    .CLK(clk), .Miss(\cache直接相联_1_miss ), .DataOut(\cache直接相联_1_dataout ),
    .BlockDataIn_2(exchange_logic_1_blockdatain1), .BlockDataIn_3(exchange_logic_1_blockdatain2),
    .BlockDataIn_4(exchange_logic_1_blockdatain3));
  assign Miss = Read_En ? \cache直接相联_1_miss  : 1'bz;  // Controlled_Buffer controlled_buffer_3
  Pull_Resistor #(.pull(0)) pull_resistor_2 (.node(Miss));
  or or_1 (or_1_out, Read_En, Write_En);
  ExChange_logic exchange_logic_1 (
    .Addr(controlled_buffer_1_out[17:2]), .ByteDataIn(ExChangeData), .Miss(\cache直接相联_1_miss ),
    .Enable(Read_En), .CLK(clk), .ByteAddrOut(ExChangeAddr), .BlockDataIn0(exchange_logic_1_blockdatain0),
    .BlkDataReady(RDY), .BlockDataIn1(exchange_logic_1_blockdatain1),
    .BlockDataIn2(exchange_logic_1_blockdatain2), .BlockDataIn3(exchange_logic_1_blockdatain3));
  and and_1 (and_1_out, or_1_out, is_MemAddr);
  assign controlled_buffer_4_out = and_1_out ? Address[17:2] : 16'bz;  // Controlled_Buffer controlled_buffer_4
  and and_2 (and_2_out, Miss, RDY);
  Counter #(.width(16), .max('hffff), .ongoal("wrap"), .trigger("rising"), .behavior("old")) counter_1 (
    .count(and_2_out), .Q(counter_1_q), .clk(clk));  // open: load, D, carry, clr, preset
  and and_3 (and_3_out, is_MemAddr, Write_En);
  Register #(.width(16), .trigger("rising"), .Select("low")) register_1 (
    .D(counter_1_q), .Q(MissNubmer), .clk(clk));  // open: en, clr
  assign controlled_buffer_5_out = and_3_out ? Write_Data : 32'bz;  // Controlled_Buffer controlled_buffer_5
  assign controlled_buffer_6_out = is_RomAddr ? ExChangeAddr : 16'bz;  // Controlled_Buffer controlled_buffer_6
  RAM #(.addrWidth(16), .dataWidth(32), .bus("separate"), .Select("high")) RAM (
    .addr(controlled_buffer_4_out), .din(controlled_buffer_5_out), .data(RAM_data), .str(and_3_out),
    .clk(clk), .ld(1'b1));  // open: sel, clr
  ROM #(.addrWidth(16), .dataWidth(32), .Select("high")) rom_1 (.addr(controlled_buffer_6_out), .data(rom_1_data));
  and and_4 (and_4_out, Read_En, is_MemAddr);
  assign ExChangeData = and_4_out ? RAM_data : 32'bz;  // Controlled_Buffer controlled_buffer_7
  assign ExChangeData = and_5_out ? rom_1_data : 32'bz;  // Controlled_Buffer controlled_buffer_8
  and and_5 (and_5_out, Read_En, is_RomAddr);

  // Other names for the same wires on the sheet: Addr[31:0] = Address; MissNumber[15:0] = MissNubmer;
  //   ReadData[31:0] = Read_Data; ReadEnable = Read_En; WriteData[31:0] = Write_Data; WriteEnable = Write_En

  // Notes on the sheet:
  //   输入引脚区
  //   输出引脚区
  //   二级存储器
  //   高电平为Miss
  //   contents of rom_1 (hex, n*v repeats v):
  //   0 1 2 3 4 5 6 7 8 9 a b c d e f 10 11 12 13 14 15 16 17 18 19 1a 1b 1c 1d 1e 1f 20 21 22 23 24 25 26
  //   27 28 29 2a 2b 2c 2d 2e 2f 30 31 32 33 34 35 36 37 38 39 3a 3b 3c 3d 3e 3f 40 41 42 43 44 45 46 47
  //   48 49 4a 4b 4c 4d 4e 4f 50 51 52 53 54 55 56 57 58 59 5a 5b 5c 5d 5e 5f 60 61 62 63 64 65 66 67 68
  //   69 6a 6b 6c 6d 6e 6f 70 71 72 73 74 75 76 77 78 79 7a 7b 7c 7d 7e 7f ffffff80 ffffff81 ffffff82
  //   ffffff83 ffffff84 ffffff85 ffffff86 ffffff87 ffffff88 ffffff89 ffffff8a ffffff8b ffffff8c ffffff8d
  //   ffffff8e ffffff8f ffffff90 ffffff91 ffffff92 ffffff93 ffffff94 ffffff95 ffffff96 ffffff97 ffffff98
  //   ffffff99 ffffff9a ffffff9b ffffff9c ffffff9d ffffff9e ffffff9f ffffffa0 ffffffa1 ffffffa2 ffffffa3
  //   ffffffa4 ffffffa5 ffffffa6 ffffffa7 ffffffa8 ffffffa9 ffffffaa ffffffab ffffffac ffffffad ffffffae
  //   ffffffaf ffffffb0 ffffffb1 ffffffb2 ffffffb3 ffffffb4 ffffffb5 ffffffb6 ffffffb7 ffffffb8 ffffffb9
  //   ffffffba ffffffbb ffffffbc ffffffbd ffffffbe ffffffbf ffffffc0 ffffffc1 ffffffc2 ffffffc3 ffffffc4
  //   ffffffc5 ffffffc6 ffffffc7 ffffffc8 ffffffc9 ffffffca ffffffcb ffffffcc ffffffcd ffffffce ffffffcf
  //   ffffffd0 ffffffd1 ffffffd2 ffffffd3 ffffffd4 ffffffd5 ffffffd6 ffffffd7 ffffffd8 ffffffd9 ffffffda
  //   ffffffdb ffffffdc ffffffdd ffffffde ffffffdf ffffffe0 ffffffe1 ffffffe2 ffffffe3 ffffffe4 ffffffe5
  //   ffffffe6 ffffffe7 ffffffe8 ffffffe9 ffffffea ffffffeb ffffffec ffffffed ffffffee ffffffef fffffff0
  //   fffffff1 fffffff2 fffffff3 fffffff4 fffffff5 fffffff6 fffffff7 fffffff8 fffffff9 fffffffa fffffffb
  //   fffffffc fffffffd fffffffe ffffffff 0 1 2 3 4 5 6 7 8 9 a b c d e f 10 11 12 13 14 15 16 17 18 19 1a
  //   1b 1c 1d 1e 1f 20 21 22 23 24 25 26 27 28 29 2a 2b 2c 2d 2e 2f 30 31 32 33 34 35 36 37 38 39 3a 3b
  //   3c 3d 3e 3f 40 41 42 43 44 45 46 47 48 49 4a 4b 4c 4d 4e 4f 50 51 52 53 54 55 56 57 58 59 5a 5b 5c
  //   5d 5e 5f 60 61 62 63 64 65 66 67 68 69 6a 6b 6c 6d 6e 6f 70 71 72 73 74 75 76 77 78 79 7a 7b 7c 7d
  //   7e 7f ffffff80 ffffff81 ffffff82 ffffff83 ffffff84 ffffff85 ffffff86 ffffff87 ffffff88 ffffff89
  //   ffffff8a ffffff8b ffffff8c ffffff8d ffffff8e ffffff8f ffffff90 ffffff91 ffffff92 ffffff93 ffffff94
  //   ffffff95 ffffff96 ffffff97 ffffff98 ffffff99 ffffff9a ffffff9b ffffff9c ffffff9d ffffff9e ffffff9f
  //   ffffffa0 ffffffa1 ffffffa2 ffffffa3 ffffffa4 ffffffa5 ffffffa6 ffffffa7 ffffffa8 ffffffa9 ffffffaa
  //   ffffffab ffffffac ffffffad ffffffae ffffffaf ffffffb0 ffffffb1 ffffffb2 ffffffb3 ffffffb4 ffffffb5
  //   ffffffb6 ffffffb7 ffffffb8 ffffffb9 ffffffba ffffffbb ffffffbc ffffffbd ffffffbe ffffffbf ffffffc0
  //   ffffffc1 ffffffc2 ffffffc3 ffffffc4 ffffffc5 ffffffc6 ffffffc7 ffffffc8 ffffffc9 ffffffca ffffffcb
  //   ffffffcc ffffffcd ffffffce ffffffcf ffffffd0 ffffffd1 ffffffd2 ffffffd3 ffffffd4 ffffffd5 ffffffd6
  //   ffffffd7 ffffffd8 ffffffd9 ffffffda ffffffdb ffffffdc ffffffdd ffffffde ffffffdf ffffffe0 ffffffe1
  //   ffffffe2 ffffffe3 ffffffe4 ffffffe5 ffffffe6 ffffffe7 ffffffe8 ffffffe9 ffffffea ffffffeb ffffffec
  //   ffffffed ffffffee ffffffef fffffff0 fffffff1 fffffff2 fffffff3 fffffff4 fffffff5 fffffff6 fffffff7
  //   fffffff8 fffffff9 fffffffa fffffffb fffffffc fffffffd fffffffe ffffffff 0 1 2 3 4 5 6 7 8 9 a b c d
  //   e f 10 11 12 13 14 15 16 17 18 19 1a 1b 1c 1d 1e 1f 20 21 22 23 24 25 26 27 28 29 2a 2b 2c 2d 2e 2f
  //   30 31 32 33 34 35 36 37 38 39 3a 3b 3c 3d 3e 3f 40 41 42 43 44 45 46 47 48 49 4a 4b 4c 4d 4e 4f 50
  //   51 52 53 54 55 56 57 58 59 5a 5b 5c 5d 5e 5f 60 61 62 63 64 65 66 67 68 69 6a 6b 6c 6d 6e 6f 70 71
  //   72 73 74 75 76 77 78 79 7a 7b 7c 7d 7e 7f ffffff80 ffffff81 ffffff82 ffffff83 ffffff84 ffffff85
  //   ffffff86 ffffff87 ffffff88 ffffff89 ffffff8a ffffff8b ffffff8c ffffff8d ffffff8e ffffff8f ffffff90
  //   ffffff91 ffffff92 ffffff93 ffffff94 ffffff95 ffffff96 ffffff97 ffffff98 ffffff99 ffffff9a ffffff9b
  //   ffffff9c ffffff9d ffffff9e ffffff9f ffffffa0 ffffffa1 ffffffa2 ffffffa3 ffffffa4 ffffffa5 ffffffa6
  //   ffffffa7 ffffffa8 ffffffa9 ffffffaa ffffffab ffffffac ffffffad ffffffae ffffffaf ffffffb0 ffffffb1
  //   ffffffb2 ffffffb3 ffffffb4 ffffffb5 ffffffb6 ffffffb7 ffffffb8 ffffffb9 ffffffba ffffffbb ffffffbc
  //   ffffffbd ffffffbe ffffffbf ffffffc0 ffffffc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
endmodule

module \Cache直接相联  (
  input  [31:0] BlockDataIn,
  input  [31:0] BlockDataIn_2,
  input  [31:0] BlockDataIn_3,
  input  [31:0] BlockDataIn_4,
  input  [15:0] Addr,
  input  BlkDataReady,
  input  CLK,
  output Miss,
  output [31:0] DataOut
);

  wire and_1_out, L0, Valid, VALID_q;
  wire [10:0] Tag, TAG_q, TagData;
  wire [31:0] SlotData0, SlotData1, SlotData2, SlotData3, \数据块副本_2_q , \数据块副本_3_q , \数据块副本_4_q , \数据块副本_q ;

  Register #(.width(1), .trigger("rising"), .Select("low")) u_VALID (
    .D(1'b1), .en(and_1_out), .Q(VALID_q), .clk(CLK));  // open: clr
  assign Valid = L0 ? VALID_q : 1'bz;  // Controlled_Buffer controlled_buffer_1
  Register #(.width(11), .trigger("rising"), .Select("low")) u_TAG (
    .D(Tag), .en(and_1_out), .Q(TAG_q), .clk(CLK));  // open: clr
  assign TagData = L0 ? TAG_q : 11'bz;  // Controlled_Buffer controlled_buffer_2
  Register #(.width(32), .trigger("rising"), .Select("low")) \u_数据块副本  (
    .D(BlockDataIn), .en(and_1_out), .Q(\数据块副本_q ), .clk(CLK));  // open: clr
  assign SlotData0 = L0 ? \数据块副本_q  : 32'bz;  // Controlled_Buffer controlled_buffer_3
  assign SlotData1 = L0 ? \数据块副本_2_q  : 32'bz;  // Controlled_Buffer controlled_buffer_4
  Register #(.width(32), .trigger("rising"), .Select("low")) \u_数据块副本_2  (
    .D(BlockDataIn_2), .en(and_1_out), .Q(\数据块副本_2_q ), .clk(CLK));  // open: clr
  Register #(.width(32), .trigger("rising"), .Select("low")) \u_数据块副本_3  (
    .D(BlockDataIn_3), .en(and_1_out), .Q(\数据块副本_3_q ), .clk(CLK));  // open: clr
  assign SlotData2 = L0 ? \数据块副本_3_q  : 32'bz;  // Controlled_Buffer controlled_buffer_5
  Register #(.width(32), .trigger("rising"), .Select("low")) \u_数据块副本_4  (
    .D(BlockDataIn_4), .en(and_1_out), .Q(\数据块副本_4_q ), .clk(CLK));  // open: clr
  assign SlotData3 = L0 ? \数据块副本_4_q  : 32'bz;  // Controlled_Buffer controlled_buffer_6
  and and_1 (and_1_out, L0, BlkDataReady);

  // Other names for the same wires on the sheet: Blk0[31:0] = BlockDataIn; Blk1[31:0] = BlockDataIn_2;
  //   Blk2[31:0] = BlockDataIn_3; Blk3[31:0] = BlockDataIn_4; BlkReady = BlkDataReady; 字节地址[15:0] = Addr

  // Notes on the sheet:
  //   输入引脚区
  //   16位
  //   标记位
  //   有效位
  //   三态门控制多行输出
  //   行选中
  //   电路功能：利用上面给定的隧道构建8行的Cache
  //   请在下方利用上方输入输出引脚的隧道信号构建电路，ctrl+d复制选择部件
  //   请勿增改引脚，请勿修改子电路封装
  //   块数据输出
  //   块数据输出
  //   块数据输出
  //   输出引脚区
  //   cache行
  //   块数据输出
endmodule

module ExChange_logic (
  input  [15:0] Addr,
  input  [31:0] ByteDataIn,
  input  Miss,
  input  Enable,
  input  CLK,
  output [15:0] ByteAddrOut,
  output [31:0] BlockDataIn0,
  output [31:0] BlockDataIn1,
  output [31:0] BlockDataIn2,
  output [31:0] BlockDataIn3,
  output BlkDataReady
);

  wire FSM_byte0_ready, FSM_byte1_ready, FSM_byte2_ready, FSM_byte3_ready;
  wire [31:0] register_1_q, register_2_q, register_3_q, register_4_q;

  assign ByteAddrOut = FSM_byte0_ready ? {Addr[15:2], 2'b00} : 16'bz;  // Controlled_Buffer controlled_buffer_1
  ExChange_FSM FSM (
    .Clk(CLK), .Miss(Miss), .Byte0_Ready(FSM_byte0_ready), .Byte1_Ready(FSM_byte1_ready),
    .Byte2_Ready(FSM_byte2_ready), .Byte3_Ready(FSM_byte3_ready), .Byte0_Ready_2(BlkDataReady), .En(Enable));
  assign ByteAddrOut = FSM_byte1_ready ? {Addr[15:2], 2'b01} : 16'bz;  // Controlled_Buffer controlled_buffer_2
  assign ByteAddrOut = FSM_byte2_ready ? {Addr[15:2], 2'b10} : 16'bz;  // Controlled_Buffer controlled_buffer_3
  assign ByteAddrOut = FSM_byte3_ready ? {Addr[15:2], 2'b11} : 16'bz;  // Controlled_Buffer controlled_buffer_4
  Register #(.width(32), .trigger("rising"), .Select("low")) register_1 (
    .D(ByteDataIn), .en(FSM_byte0_ready), .Q(register_1_q), .clk(CLK));  // open: clr
  Register #(.width(32), .trigger("rising"), .Select("low")) register_2 (
    .D(ByteDataIn), .en(FSM_byte1_ready), .Q(register_2_q), .clk(CLK));  // open: clr
  Register #(.width(32), .trigger("rising"), .Select("low")) register_3 (
    .D(ByteDataIn), .en(FSM_byte2_ready), .Q(register_3_q), .clk(CLK));  // open: clr
  Register #(.width(32), .trigger("rising"), .Select("low")) register_4 (
    .D(ByteDataIn), .en(FSM_byte3_ready), .Q(register_4_q), .clk(CLK));  // open: clr
  assign BlockDataIn0 = BlkDataReady ? register_1_q : 32'bz;  // Controlled_Buffer controlled_buffer_5
  assign BlockDataIn1 = BlkDataReady ? register_2_q : 32'bz;  // Controlled_Buffer controlled_buffer_6
  assign BlockDataIn2 = BlkDataReady ? register_3_q : 32'bz;  // Controlled_Buffer controlled_buffer_7
  assign BlockDataIn3 = BlkDataReady ? register_4_q : 32'bz;  // Controlled_Buffer controlled_buffer_8

  // Notes on the sheet:
  //   数据缓存寄存器
endmodule

module ExChange_FSM (
  input  En,
  input  Clk,
  input  Miss,
  output Byte0_Ready,
  output Byte1_Ready,
  output Byte2_Ready,
  output Byte3_Ready,
  output Byte0_Ready_2
);

  wire and_1_out, and_2_out, and_3_out, and_4_out, and_5_out, and_6_out, and_7_out, Next_Q0, Next_Q1,
       Next_Q2, Next_Q3, not_1_out, not_2_out, not_3_out, not_4_out, not_5_out, not_6_out, not_7_out,
       not_8_out, not_9_out, not_10_out, not_11_out, not_12_out, not_13_out, or_1_out, or_2_out, Q0, Q1, Q2,
       Q3;

  not not_1 (not_1_out, Q3);
  not not_2 (not_2_out, Q3);
  not not_3 (not_3_out, Q2);
  not not_4 (not_4_out, Q3);
  not not_5 (not_5_out, Q1);
  not not_6 (not_6_out, Q3);
  not not_7 (not_7_out, Q0);
  not not_8 (not_8_out, Q3);
  not not_9 (not_9_out, Q0);
  D_Flip_Flop #(.trigger("rising"), .Pre_Clr_Positions("LEGACY"), .NegatePresetClear("false"), .enable("true"), .NewFFLayout("false")) d_ff_1 (
    .clk(Clk), .D(Next_Q3), .Q(Q3), .en(En));  // open: Qn, preset, reset
  D_Flip_Flop #(.trigger("rising"), .Pre_Clr_Positions("LEGACY"), .NegatePresetClear("false"), .enable("true"), .NewFFLayout("false")) d_ff_2 (
    .clk(Clk), .D(Next_Q2), .Q(Q2), .en(En));  // open: Qn, preset, reset
  D_Flip_Flop #(.trigger("rising"), .Pre_Clr_Positions("LEGACY"), .NegatePresetClear("false"), .enable("true"), .NewFFLayout("false")) d_ff_3 (
    .clk(Clk), .D(Next_Q1), .Q(Q1), .en(En));  // open: Qn, preset, reset
  D_Flip_Flop #(.trigger("rising"), .Pre_Clr_Positions("LEGACY"), .NegatePresetClear("false"), .enable("true"), .NewFFLayout("false")) d_ff_4 (
    .clk(Clk), .D(Next_Q0), .Q(Q0), .en(En));  // open: Qn, preset, reset
  and and_1 (and_1_out, not_1_out, Q2, Q1, Q0);
  and and_2 (and_2_out, not_2_out, not_3_out, Q1, Q0);
  not not_10 (not_10_out, Q3);
  and and_3 (and_3_out, not_10_out, Q2, not_11_out);
  not not_11 (not_11_out, Q1);
  not not_12 (not_12_out, Q3);
  and and_4 (and_4_out, not_12_out, Q2, not_13_out);
  not not_13 (not_13_out, Q0);
  and and_5 (and_5_out, not_4_out, not_5_out, Q0);
  and and_6 (and_6_out, not_6_out, Q1, not_7_out);
  and and_7 (and_7_out, not_8_out, not_9_out);
  or or_1 (or_1_out, and_2_out, and_3_out, and_4_out);
  or or_2 (or_2_out, and_5_out, and_6_out);
  Decoder #(.select(4), .tristate("false"), .disabled(0), .enable("false")) decoder_1 (
    .out1(Byte0_Ready), .out3(Byte1_Ready), .out5(Byte2_Ready), .out7(Byte3_Ready), .out8(Byte0_Ready_2),
    .sel({Q3, Q2, Q1, Q0}));  // open: out0, out2, out4, out6, out9, out10, out11, out12, out13, out14, out15
  and and_8 (Next_Q3, and_1_out, Miss);
  and and_9 (Next_Q2, or_1_out, Miss);
  and and_10 (Next_Q1, Miss, or_2_out);
  and and_11 (Next_Q0, Miss, and_7_out);
endmodule

module IF_ID (
  input  [31:0] IF_Instruction,
  input  in_2,
  input  [31:0] IF_PC,
  input  in_4,
  output [31:0] ID_Instruction,
  output [31:0] ID_PC
);

  wire and_1_out;
  wire [31:0] PC_q;

  Register #(.width(32), .trigger("rising"), .Select("low")) PC (
    .D(IF_Instruction), .en(1'b1), .Q(PC_q), .clk(in_2), .clr(in_4));
  Multiplexer #(.select(1), .width(32), .disabled("Z"), .enable("false")) multiplexer_1 (
    .in0(PC_q), .in1({32{1'b0}}), .out(ID_Instruction), .sel(and_1_out));
  and and_1 (and_1_out, in_2, in_4);

  assign ID_PC = IF_PC;
endmodule

module ID_EX (
  input  [2:0] in_1,
  input  in_2,
  input  in_3,
  input  in_4,
  input  in_5,
  input  in_6,
  input  in_7,
  input  in_8,
  input  [1:0] in_9,
  input  in_10,
  input  in_11,
  input  [3:0] in_12,
  input  in_13,
  input  in_14,
  input  in_15,
  input  in_16,
  input  in_17,
  input  in_18,
  input  [31:0] in_19,
  output [2:0] out_20,
  output out_21,
  output out_22,
  output out_23,
  output out_24,
  output out_25,
  output out_26,
  output out_27,
  output [1:0] out_28,
  output out_29,
  output out_30,
  output [3:0] out_31,
  output out_32,
  output out_33,
  output out_34,
  output out_35,
  output [31:0] out_36
);

  wire PC_2_q, PC_3_q, PC_4_q, PC_5_q, PC_6_q, PC_7_q, PC_8_q, PC_10_q, PC_11_q, PC_13_q, PC_14_q, PC_15_q,
       PC_16_q;
  wire [1:0] PC_9_q;
  wire [2:0] PC_q;
  wire [3:0] PC_12_q;
  wire [31:0] PC_17_q;

  Register #(.width(3), .trigger("rising"), .Select("low")) PC (
    .D(in_1), .en(1'b1), .Q(PC_q), .clk(in_17), .clr(in_18));
  Register #(.width(1), .trigger("rising"), .Select("low")) PC_2 (
    .D(in_2), .en(1'b1), .Q(PC_2_q), .clk(in_17), .clr(in_18));
  Register #(.width(1), .trigger("rising"), .Select("low")) PC_3 (
    .D(in_3), .en(1'b1), .Q(PC_3_q), .clk(in_17), .clr(in_18));
  Register #(.width(1), .trigger("rising"), .Select("low")) PC_4 (
    .D(in_4), .en(1'b1), .Q(PC_4_q), .clk(in_17), .clr(in_18));
  Register #(.width(1), .trigger("rising"), .Select("low")) PC_5 (
    .D(in_5), .en(1'b1), .Q(PC_5_q), .clk(in_17), .clr(in_18));
  Register #(.width(1), .trigger("rising"), .Select("low")) PC_6 (
    .D(in_6), .en(1'b1), .Q(PC_6_q), .clk(in_17), .clr(in_18));
  Register #(.width(1), .trigger("rising"), .Select("low")) PC_7 (
    .D(in_7), .en(1'b1), .Q(PC_7_q), .clk(in_17), .clr(in_18));
  Register #(.width(1), .trigger("rising"), .Select("low")) PC_8 (
    .D(in_8), .en(1'b1), .Q(PC_8_q), .clk(in_17), .clr(in_18));
  Register #(.width(2), .trigger("rising"), .Select("low")) PC_9 (
    .D(in_9), .en(1'b1), .Q(PC_9_q), .clk(in_17), .clr(in_18));
  Register #(.width(1), .trigger("rising"), .Select("low")) PC_10 (
    .D(in_10), .en(1'b1), .Q(PC_10_q), .clk(in_17), .clr(in_18));
  Register #(.width(1), .trigger("rising"), .Select("low")) PC_11 (
    .D(in_11), .en(1'b1), .Q(PC_11_q), .clk(in_17), .clr(in_18));
  Register #(.width(4), .trigger("rising"), .Select("low")) PC_12 (
    .D(in_12), .en(1'b1), .Q(PC_12_q), .clk(in_17), .clr(in_18));
  Register #(.width(1), .trigger("rising"), .Select("low")) PC_13 (
    .D(in_13), .en(1'b1), .Q(PC_13_q), .clk(in_17), .clr(in_18));
  Register #(.width(1), .trigger("rising"), .Select("low")) PC_14 (
    .D(in_14), .en(1'b1), .Q(PC_14_q), .clk(in_17), .clr(in_18));
  Register #(.width(1), .trigger("rising"), .Select("low")) PC_15 (
    .D(in_15), .en(1'b1), .Q(PC_15_q), .clk(in_17), .clr(in_18));
  Register #(.width(1), .trigger("rising"), .Select("low")) PC_16 (
    .D(in_16), .en(1'b1), .Q(PC_16_q), .clk(in_17), .clr(in_18));
  Register #(.width(32), .trigger("rising"), .Select("low")) PC_17 (
    .D(in_19), .en(1'b1), .Q(PC_17_q), .clk(in_17), .clr(in_18));
  Multiplexer #(.select(1), .width(32), .disabled("Z"), .enable("false")) multiplexer_1 (
    .in0(PC_17_q), .in1({32{1'b0}}), .out(out_36), .sel(in_18));
  Multiplexer #(.select(1), .width(3), .disabled("Z"), .enable("false")) multiplexer_2 (
    .in0(PC_q), .in1(3'b000), .out(out_20), .sel(in_18));
  Multiplexer #(.select(1), .width(1), .disabled("Z"), .enable("false")) multiplexer_3 (
    .in0(PC_2_q), .in1(1'b0), .out(out_21), .sel(in_18));
  Multiplexer #(.select(1), .width(1), .disabled("Z"), .enable("false")) multiplexer_4 (
    .in0(PC_3_q), .in1(1'b0), .out(out_22), .sel(in_18));
  Multiplexer #(.select(1), .width(1), .disabled("Z"), .enable("false")) multiplexer_5 (
    .in0(PC_4_q), .in1(1'b0), .out(out_23), .sel(in_18));
  Multiplexer #(.select(1), .width(1), .disabled("Z"), .enable("false")) multiplexer_6 (
    .in0(PC_5_q), .in1(1'b0), .out(out_24), .sel(in_18));
  Multiplexer #(.select(1), .width(1), .disabled("Z"), .enable("false")) multiplexer_7 (
    .in0(PC_6_q), .in1(1'b0), .out(out_25), .sel(in_18));
  Multiplexer #(.select(1), .width(1), .disabled("Z"), .enable("false")) multiplexer_8 (
    .in0(PC_7_q), .in1(1'b0), .out(out_26), .sel(in_18));
  Multiplexer #(.select(1), .width(1), .disabled("Z"), .enable("false")) multiplexer_9 (
    .in0(PC_8_q), .in1(1'b0), .out(out_27), .sel(in_18));
  Multiplexer #(.select(1), .width(2), .disabled("Z"), .enable("false")) multiplexer_10 (
    .in0(PC_9_q), .in1(2'b00), .out(out_28), .sel(in_18));
  Multiplexer #(.select(1), .width(1), .disabled("Z"), .enable("false")) multiplexer_11 (
    .in0(PC_10_q), .in1(1'b0), .out(out_29), .sel(in_18));
  Multiplexer #(.select(1), .width(1), .disabled("Z"), .enable("false")) multiplexer_12 (
    .in0(PC_11_q), .in1(1'b0), .out(out_30), .sel(in_18));
  Multiplexer #(.select(1), .width(4), .disabled("Z"), .enable("false")) multiplexer_13 (
    .in0(PC_12_q), .in1(4'b0000), .out(out_31), .sel(in_18));
  Multiplexer #(.select(1), .width(1), .disabled("Z"), .enable("false")) multiplexer_14 (
    .in0(PC_13_q), .in1(1'b0), .out(out_32), .sel(in_18));
  Multiplexer #(.select(1), .width(1), .disabled("Z"), .enable("false")) multiplexer_15 (
    .in0(PC_14_q), .in1(1'b0), .out(out_33), .sel(in_18));
  Multiplexer #(.select(1), .width(1), .disabled("Z"), .enable("false")) multiplexer_16 (
    .in0(PC_15_q), .in1(1'b0), .out(out_34), .sel(in_18));
  Multiplexer #(.select(1), .width(1), .disabled("Z"), .enable("false")) multiplexer_17 (
    .in0(PC_16_q), .in1(1'b0), .out(out_35), .sel(in_18));
endmodule
